# Fritzing sketch BoardDesign (saved by Fritzing 0.8.7b)
breadboards: 1

parts:
  R1 = Resistor [tolerance=±5% resistance=330 package=THT]
  LED1 = LED - 5mm [color="Red (633nm)" package="5 mm [THT]"]
  Part1 = Arduino Mega 2560 (Rev3)  # not connected
  Part2 = Arduino Ethernet Shield (Rev3)
  R2 = Temperature Sensor (Thermistor) [thermistor_type=NTC package=THT]
  R3 = Resistor [tolerance=±5% resistance=10k package=THT]

nets:
  N1: R1.Pin_0, LED1.anode
  N2: R1.Pin_1, Part2.D2
  N3: LED1.cathode, Part2.GND, R3.Pin_0
  N4: Part2.A0, R2.pin_1, R3.Pin_1
  N5: Part2.5V, R2.pin_0

notes:
  330 Ohm
  10kOhm
